# Fritzing sketch Button (saved by Fritzing 0.9.3b)
breadboards: 1

parts:
  Componente1 = Arduino Nano (Rev3.0)
  Q1 = NPN-Transistor [package="TO92 [THT]"]
  Q2 = NPN-Transistor [package="TO92 [THT]"]
  R1 = Resistor [tolerance=±5% resistance=10k package=THT]
  R2 = Resistor [tolerance=±5% resistance=10k package=THT]
  S1 = Pushbutton [package="[THT]"]
  S2 = Pushbutton [package="[THT]"]
  R3 = Resistor [tolerance=±5% resistance=220 package=THT]
  LED1 = LED - 5mm [color="Red (633nm)" package="5 mm [THT]"]

nets:
  N1: Componente1.GND, LED1.cathode
  N2: Componente1.D5, Q1.B, R1.Pin_0
  N3: Componente1.D7, Componente1.5V, Q1.C, Q2.C, R1.Pin_1, R2.Pin_1, S1.Pin_3, S1.Pin_4, S2.Pin_3, S2.Pin_4
  N4: Q1.E, Q2.E, R3.Pin_0
  N5: Q2.B, R2.Pin_0
  N6: S1.Pin_1, S1.Pin_2
  N7: S2.Pin_1, S2.Pin_2
  N8: R3.Pin_1, LED1.anode
